# Fritzing sketch schematic (saved by Fritzing 0.9.3b)
breadboards: 1

parts:
  R1 = Photocell (LDR) [package=THT]
  R2 = Photocell (LDR) [package=THT]
  R3 = Resistor [tolerance=±5% resistance=10k package="0603 [SMD]"]
  R4 = Resistor [tolerance=±5% resistance=10k package="0603 [SMD]"]
  Part1 = Arduino Uno (Rev3) - ICSP
  Part2 = DeuLigne 1.1 - The Snootlab's LCD shield for Arduino  # not connected

nets:
  N1: R1.pin_0, R2.pin_1, Part1.5V
  N2: R1.pin_1, R3.Pin_0, Part1.A0
  N3: R2.pin_0, R4.Pin_1, Part1.A1
  N4: R3.Pin_1, R4.Pin_0, Part1.GND
